# Fritzing sketch fmri_response3r3 (saved by Fritzing 0.7.4b)
breadboards: 1

parts:
  Teensy2_0 = Teensy 2.0
  Rx1 = IC, DIP package, 8 pins [chip_label=Rx1 spacing=300mil]
  C1 = Ceramic Capacitor [capacitance=100nF package="100 mil [THT, multilayer]"]
  Rx3 = IC, DIP package, 8 pins [chip_label=Rx3 spacing=300mil]
  Rx4 = IC, DIP package, 8 pins [chip_label=Rx4 spacing=300mil]
  Rx5 = IC, DIP package, 8 pins [chip_label=Rx5 spacing=300mil]
  Rx2 = IC, DIP package, 8 pins [chip_label=Rx2 spacing=300mil]
  C2 = Ceramic Capacitor [capacitance=100nF package="100 mil [THT, multilayer]"]
  C3 = Ceramic Capacitor [capacitance=100nF package="100 mil [THT, multilayer]"]
  C4 = Ceramic Capacitor [capacitance=100nF package="100 mil [THT, multilayer]"]
  C5 = Ceramic Capacitor [capacitance=100nF package="100 mil [THT, multilayer]"]
  Tx1 = IC, DIP package, 8 pins [chip_label=Tx1 spacing=300mil]
  Tx2 = IC, DIP package, 8 pins [chip_label=Tx2 spacing=300mil]
  Tx3 = IC, DIP package, 8 pins [chip_label=Tx3 spacing=300mil]
  Tx4 = IC, DIP package, 8 pins [chip_label=Tx4 spacing=300mil]
  Tx5 = IC, DIP package, 8 pins [chip_label=Tx5 spacing=300mil]
  100x5 = female pin header, 6 pins [form="♀ (female)"]
  IO_Dig = shrouded pin header, 16 pins [form="♂ (shrouded male)"]
  330x8 = female pin header, 9 pins [form="♀ (female)"]
  RxTrig = IC, DIP package, 8 pins [chip_label=RxTrig spacing=300mil]
  C6 = Ceramic Capacitor [capacitance=100nF package="100 mil [THT, multilayer]"]
  1Mx5 = female pin header, 6 pins [form="♀ (female)"]
  100K = Resistor [tolerance=±5% resistance=100k package=THT]
  TLC555 = 555 Timer [package="DIP8 [THT]"]
  LED = LED - 5mm [color="Red (633nm)" package="5 mm [THT]"]
  1K = Resistor [tolerance=±5% resistance=220 package=THT]
  103 = Ceramic Capacitor [capacitance=100nF part_number=103 package="100 mil [THT, multilayer]"]
  220K = Resistor [tolerance=±5% resistance=220k package=THT]
  104 = Ceramic Capacitor [capacitance=100nF part_number=104 package="100 mil [THT, multilayer]"]

nets:
  N1: Teensy2_0.GND, Rx1.pin2, C1.0, Rx3.pin2, Rx4.pin2, Rx5.pin2, Rx2.pin2, C2.0, C3.0, C4.0, C5.0, Tx1.pin2, Tx2.pin2, Tx3.pin2, Tx4.pin2, Tx5.pin2, 330x8.pin1, RxTrig.pin2, C6.0, TLC555.Ground, 103.1, 104.0
  N2: Teensy2_0.B0, IO_Dig.pin16
  N3: Teensy2_0.B1, IO_Dig.pin15
  N4: Teensy2_0.B2, IO_Dig.pin14
  N5: Teensy2_0.B3, IO_Dig.pin13
  N6: Teensy2_0.B7, IO_Dig.pin12
  N7: Teensy2_0.D0, IO_Dig.pin11
  N8: Teensy2_0.D1, IO_Dig.pin10
  N9: Teensy2_0.D2, IO_Dig.pin9
  N10: Teensy2_0.F7, TLC555.Output, LED.cathode
  N11: Teensy2_0.F6, Rx5.pin1, 1Mx5.pin6
  N12: Teensy2_0.F5, Rx4.pin1, 1Mx5.pin5
  N13: Teensy2_0.F4, Rx3.pin1, 1Mx5.pin4
  N14: Teensy2_0.F1, Rx2.pin1, 1Mx5.pin3
  N15: Teensy2_0.F0, Rx1.pin1, 1Mx5.pin2
  N16: Teensy2_0.VCC, Rx1.pin3, C1.1, Rx3.pin3, Rx4.pin3, Rx5.pin3, Rx2.pin3, C2.1, C3.1, C4.1, C5.1, 100x5.pin1, RxTrig.pin3, C6.1, 1Mx5.pin1, 100K.Pin_1, TLC555.Reset, TLC555.Vcc_Supply_Voltage, 1K.Pin_0, 220K.Pin_0
  N17: Tx1.pin1, Tx1.pin8, 100x5.pin6
  N18: Tx2.pin1, Tx2.pin8, 100x5.pin5
  N19: Tx3.pin1, Tx3.pin8, 100x5.pin4
  N20: Tx4.pin1, 100x5.pin3
  N21: Tx5.pin1, 100x5.pin2
  N22: IO_Dig.pin1, 330x8.pin2
  N23: IO_Dig.pin2, 330x8.pin3
  N24: IO_Dig.pin3, 330x8.pin4
  N25: IO_Dig.pin4, 330x8.pin5
  N26: IO_Dig.pin5, 330x8.pin6
  N27: IO_Dig.pin6, 330x8.pin7
  N28: IO_Dig.pin7, 330x8.pin8
  N29: IO_Dig.pin8, 330x8.pin9
  N30: RxTrig.pin1, 100K.Pin_0, TLC555.Trigger
  N31: TLC555.Control_Voltage, 103.0
  N32: TLC555.Threshold, TLC555.Discharge, 220K.Pin_1, 104.1
  N33: LED.anode, 1K.Pin_1

notes:
  www.mricro.com
  fritzing.org
  fMRI optical response device
  Rx=2524 Tx=1524 Cn=104
